# Fritzing sketch P2000 (saved by Fritzing 0.9.4)
circuit board: 8.46667cm x 5.64444cm
breadboards: 1

parts:
  Composant1 = Arduino Nano (Rev3.0)
  S1 = Round Pushbutton
  S2 = Round Pushbutton
  S3 = Taiway 100-SP-X-T1 SPDT Miniature Toggle Switch [part_number=100-SP-X-T1-0-0-B1-M1 package=THT]
  LED1 = LEDs [package=led10mm]
  Driver1 = 28BYJ-48 Driver Module [part_number=ULN2003 package=THT]
  SM1 = 28BYJ-48 Stepper Motor [part_number=28BYJ-48]
  R1 = Resistor [tolerance=±5% resistance=220 package="0603 [SMD]"]
  Composant2 = Real Time Clock Module - DS1307 RTC Breakout Board

nets:
  N1: Composant1.D2, S1.leg0
  N2: Composant1.D3, S2.leg0
  N3: Composant1.D4, Driver1.IN1
  N4: Composant1.D5, Driver1.IN2
  N5: Composant1.D6, Driver1.IN3
  N6: Composant1.D7, Driver1.IN4
  N7: Composant1.D8, S3.COM
  N8: Composant1.D9, R1.Pin_1
  N9: Composant1.A2, Composant2.SDA
  N10: Composant1.A1, Composant2.SCL
  N11: Composant1.A0, Composant2.SQW
  GND: S1.leg1, S2.leg1, S3.L1, LED1.C, Driver1.GND, Composant2.GND
  N12: S3.L2, Driver1.Vmotor, Composant2.5V
  N13: LED1.A, R1.Pin_0
  N14: Driver1.blue-pin, SM1.blue-pin
  N15: Driver1.pink-pin, SM1.pink-pin
  N16: Driver1.yellow-pin, SM1.yellow-pin
  N17: Driver1.orange-pin, SM1.orange-pin
  N18: Driver1.red-pin, SM1.red-pin

custom parts:
  28BYJ-48 Driver Module: ULN2003 Driver Module for the 28BYJ-48 Unipolar Stepper Motor LED A - Blue wire - Bottom coil left LED B - Pink wire - Top coil left LED C - Yellow wire - Bottom coil right LED D - Orange wire - Top coil right Common rail - red Connector pins: blue - pink - yellow - orange - red Control pins - IN1 to IN4 Power pins - GND & Vmotor (5-12V) On/Off jumper (if removed, power to motor is cut).
  28BYJ-48 Stepper Motor: Unipolar Stepper Motor 28BYJ-48 Top coil - pink & orange Bottom coil - blue & yellow Common rail - red Connector pins: blue - pink - yellow - orange - red
